# Fritzing sketch Home Auto (saved by Fritzing 0.9.3b)
breadboards: 1

parts:
  Part1 = Arduino Uno (Rev3)
  M1 = fc-51 [package=THT]
  J1 = Piezo Speaker
  M2 = fc-51 [package=THT]
  KY-1 = Keyes Relay [package=THT]
  KY-2 = Keyes Relay [package=THT]
  Part2 = HC-05 [part_number=HC-05 package="breakout board"]

nets:
  N1: Part1.D0/RX, Part2.TXD
  N2: Part1.D1/TX, Part2.RXD
  N3: Part1.D2, M1.pin1
  N4: Part1.D3_PWM, J1.pin2
  N5: Part1.D4, M2.pin1
  N6: Part1.D5_PWM, KY-1.signal
  N7: Part1.D6_PWM, KY-2.signal
  5V: Part1.5V, M1.pin3, M2.pin3, KY-1.power, KY-2.power, Part2.VCC
  GND: Part1.GND, M1.pin2, J1.pin1, M2.pin2, KY-1.ground, KY-2.ground, Part2.GND

custom parts:
  Keyes Relay: The Keyes 5V relay module is suitable for SCM development, home appliance control. It uses a 5V~12V TIL control signal which can control DC / AC signal.
  HC-05: A commonly available HC-05 Bluetooth breakout board.
